// Logisim project TallerLogica-Combinatorios.circ as structural Verilog: 9 circuits, main circuit verificador
module sumador_simple (
  input  a,
  input  b,
  output S,
  output Cout
);
endmodule

module sumador_completo (
  input  Cin,
  input  A,
  input  B,
  output S,
  output Cout
);
endmodule

module sumador_4 (
  input  Cin,
  input  [3:0] A,
  input  [3:0] B,
  output [3:0] S,
  output Cout
);

  Hex_Digit_Display hex_digit_display_1 (.value(S));  // open: dp
endmodule

module comparador_cero (
  input  [3:0] A,
  output Z
);
endmodule

module sumador_flags (
  input  Cin,
  input  [3:0] A,
  input  [3:0] B,
  output [3:0] S,
  output N,
  output Z,
  output V,
  output C
);

  Hex_Digit_Display hex_digit_display_1 (.value(S));  // open: dp
endmodule

module incrementador_4 (
  input  [3:0] A,
  output [3:0] S
);

  Hex_Digit_Display hex_digit_display_1 (.value(S));  // open: dp
endmodule

module inversor_4 (
  input  [3:0] A,
  input  INV,
  output [3:0] S
);

  Hex_Digit_Display hex_digit_display_1 (.value(S));  // open: dp
endmodule

module ALU (
  input  [3:0] A,
  input  [3:0] B,
  input  [1:0] OP,
  output N,
  output Z,
  output V,
  output C,
  output [3:0] S
);

  Hex_Digit_Display hex_digit_display_1 (.value(S));  // open: dp
endmodule

module verificador (
  output [3:0] a,
  output [3:0] b,
  output [1:0] Op,
  output N,
  output Z,
  output V,
  output C,
  output [3:0] Res,
  output halt
);

  wire clock_1_out;

  Clock clock_1 (.out(clock_1_out));
  Counter #(.width(10), .max('h3ff)) counter_1 (
    .Q({Op, b, a}), .carry(halt), .clk(clock_1_out));  // open: load, D, count, clr
  ALU alu_1 (.A(a), .B(b), .OP(Op), .N(N), .Z(Z), .V(V), .C(C), .S(Res));
endmodule
